# Fritzing sketch carlosLight_v3.01 (saved by Fritzing 0.9.3b)
circuit board: 6.48541cm x 14.9266cm
breadboards: 1

parts:
  C4_1kµF = Electrolytic Capacitor [capacitance=1000µF package="300 mil [THT, electrolytic]"]
  DOut = Header 1 [package=smtso-256-et]
  VIn = Header 1 [package=smtso-256-et]
  GNDIn = Header 1 [package=smtso-256-et]
  VOut = Header 1 [package=smtso-256-et]
  GNDOut = Header 1 [package=smtso-256-et]
  Vout = Header 1 [package=smtso-256-et]
  GNDIn_2 = Header 1 [package=smtso-256-et]
  VIn_2 = Header 1 [package=smtso-256-et]
  GNDOut_2 = Header 1 [package=smtso-256-et]
  Vin = Header 1 [package=smtso-256-et]
  VOut_2 = Header 1 [package=smtso-256-et]
  GNDIn_3 = Header 1 [package=smtso-256-et]
  C2_1kµF = Electrolytic Capacitor [capacitance=1000µF package="300 mil [THT, electrolytic]"]
  C1_1kµF = Electrolytic Capacitor [capacitance=1000µF package="300 mil [THT, electrolytic]"]
  C3_1kµF1 = Electrolytic Capacitor [capacitance=1000µF package="300 mil [THT, electrolytic]"]
  GNDOut_3 = Header 1 [package=smtso-256-et]
  GNDOut_4 = Header 1 [package=smtso-256-et]
  VOut1 = Header 1 [package=smtso-256-et]
  VIn1 = Header 1 [package=smtso-256-et]
  JP2 = Header 12 [part_number=1 package=1x12_machine-pin-header_lock.004]
  U4 = Header 12 [part_number=u1 package=1x12_machine-pin-header_lock.004]
  U5 = Header 12 [part_number=u2 package=1x12_machine-pin-header_lock.004]
  U6 = Header 12 [part_number=u3 package=1x12_machine-pin-header_lock.004]  # not connected
  JP3 = Header 12 [part_number=u4 package=1x12_machine-pin-header_lock.004]
  JP4 = Header 12 [part_number=u5 package=1x12_machine-pin-header_lock.004]  # not connected
  JP5 = Header 12 [part_number=u6+3 package=1x12_machine-pin-header_lock.004]
  JP6 = Header 12 [part_number=2 package=1x12_machine-pin-header_lock.004]
  JP7 = Header 12 [part_number=3+1 package=1x12_machine-pin-header_lock.004]
  GNDIn_4 = Header 1 [package=smtso-256-et]
  Standby = smd LED [color="Red (633nm)" package="1206 [SMD]"]
  U1 = SPST Switch [package=switch-spdt_kit]
  R330 = Resistor [tolerance=±5% resistance=330 power=5 package="1206 [SMD]"]
  R470 = Resistor [tolerance=±5% resistance=470 power=5 package="1206 [SMD]"]

nets (from the pcb view):
  N1: C4_1kµF.-, GNDIn.1, GNDOut.1, GNDIn_2.1, GNDOut_2.1, GNDIn_3.1, C2_1kµF.-, C1_1kµF.-, C3_1kµF1.-, GNDOut_3.1, GNDOut_4.1, JP2.2, JP6.2, JP7.11, GNDIn_4.1, R330.Pin_0
  N2: C4_1kµF.+, VIn.1, VOut.1, Vout.1, VIn_2.1, Vin.1, VOut_2.1, C2_1kµF.+, C1_1kµF.+, C3_1kµF1.+, VOut1.1, VIn1.1, U1.P
  N3: DOut.1, R470.Pin_0
  N4: JP2.1, JP6.3, JP7.12, U1.O
  N5: U4.11, U5.11, JP3.11, JP5.11, JP6.8, R470.Pin_1
  N6: Standby.cathode, R330.Pin_1
  N7: Standby.anode, U1.S
