# Fritzing sketch tvbacklight_v2.0 (saved by Fritzing 0.9.3b)
circuit board: 14cm x 8cm
breadboards: 1

parts:
  C1_1kµF = Electrolytic Capacitor [capacitance=1000µF package="300 mil [THT, electrolytic]"]
  GNDIn = Header 1 [package=smtso-256-et]
  DOut = Header 1 [package=smtso-256-et]
  VIn = Header 1 [package=smtso-256-et]
  GNDIn_2 = Header 1 [package=smtso-256-et]
  VOut = Header 1 [package=smtso-256-et]
  GNDOut = Header 1 [package=smtso-256-et]
  Vout = Header 1 [package=smtso-256-et]
  GNDIn_3 = Header 1 [package=smtso-256-et]
  VIn_2 = Header 1 [package=smtso-256-et]
  GNDOut_2 = Header 1 [package=smtso-256-et]
  Vin = Header 1 [package=smtso-256-et]
  VOut_2 = Header 1 [package=smtso-256-et]
  GNDOut_3 = Header 1 [package=smtso-256-et]
  C2_1kµF = Electrolytic Capacitor [capacitance=1000µF package="300 mil [THT, electrolytic]"]
  C3_1kµF = Electrolytic Capacitor [capacitance=1000µF package="300 mil [THT, electrolytic]"]
  R470 = Resistor [tolerance=±5% resistance=470 power=5 package=THT]
  C4_1kµF1 = Electrolytic Capacitor [capacitance=1000µF package="300 mil [THT, electrolytic]"]  # not connected
  GNDIn1 = Header 1 [package=smtso-256-et]  # not connected
  GNDOut_4 = Header 1 [package=smtso-256-et]  # not connected
  VOut1 = Header 1 [package=smtso-256-et]  # not connected
  VIn1 = Header 1 [package=smtso-256-et]  # not connected
  U1 = SWITCH_SPDT [package=kps-1290]
  NodeMCU_v1 = NodeMCU v3 LoLin [part_number=ESP8266]  # not connected
  U2 = LuaNode32 / ESP32  # not connected
  U3 = NodeMCU V1.0  # not connected
  JP2 = Header 12 [package=1x12_machine-pin-header_lock.004]
  Bauteil1 = Arduino Nano (Rev3.0)  # not connected
  U4 = Header 12 [package=1x12_machine-pin-header_lock.004]
  U5 = Header 12 [package=1x12_machine-pin-header_lock.004]
  U6 = Header 12 [package=1x12_machine-pin-header_lock.004]
  JP3 = Header 12 [package=1x12_machine-pin-header_lock.004]
  JP4 = Header 12 [package=1x12_machine-pin-header_lock.004]  # not connected
  JP5 = Header 12 [package=1x12_machine-pin-header_lock.004]
  JP6 = Header 12 [package=1x12_machine-pin-header_lock.004]
  M1 = STM32F103C8T6 blue mini board  # not connected
  JP7 = Header 12 [package=1x12_machine-pin-header_lock.004]
  WeMos_D1_Mini1 = WeMos D1 Mini  # not connected

nets (from the breadboard view):
  N1: C1_1kµF.-, GNDIn.1, GNDIn_2.1, GNDOut.1, GNDIn_3.1, GNDOut_2.1, GNDOut_3.1, C2_1kµF.-, C3_1kµF.-, JP2.2, JP6.2, JP7.11
  N2: C1_1kµF.+, VIn.1, VOut.1, VIn_2.1, VOut_2.1, C2_1kµF.+, U1.S
  N3: DOut.1, R470.Pin_0
  N4: Vout.1, Vin.1, C3_1kµF.+
  N5: R470.Pin_1, U4.11, U5.11, U6.11, JP3.11, JP5.11, JP6.8
  N6: U1.P, JP2.1, JP6.3, JP7.12

custom parts:
  NodeMCU v3 LoLin: NodeMCU v3 LoLin NodeMCU (http://www.nodemcu.com/) is an open source IoT platform. It includes firmware (https://nodemcu-build.com/) which runs on the ESP8266 Wi-Fi SoC from Espressif Systems, and hardware which is based on the ESP-12E module. The term "NodeMCU" by default refers to the firmware rather than the dev kits. The firmware uses the Lua scripting language. It is based on the eLua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
  LuaNode32 / ESP32: ESP32 based LuaNode32
  NodeMCU V1.0: ESP8266 based NodeMCU
  WeMos D1 Mini: The D1 mini is a mini wifi board based on ESP-8266EX.
